// Logisim project roll no.9 batch-B1 sub-COD.circ as structural Verilog
module main (
  input  A,
  input  B,
  input  C,
  output D
);

  wire nand_1_out, not_1_out;

  not not_1 (not_1_out, C);
  nand nand_1 (nand_1_out, A, B);
  or or_1 (D, nand_1_out, not_1_out);
endmodule

module Que_4_i (
  input  A,
  input  B,
  input  C,
  output X
);

  wire and_1_out, nor_1_out;

  nor nor_1 (nor_1_out, A, B);
  and and_1 (and_1_out, B, C);
  or or_1 (X, nor_1_out, and_1_out);
endmodule

module _4_ii (
  input  A,
  input  B,
  input  C,
  output D
);

  wire not_1_out, or_1_out;

  or or_1 (or_1_out, A, B);
  not not_1 (not_1_out, C);
  and and_1 (D, or_1_out, not_1_out);
endmodule

module Que_6 (
  input  A,
  input  B,
  input  C,
  output D
);

  and and_1 (D, A, B, C);
endmodule

module QUE_7_i (
  input  A,
  input  B,
  input  C,
  output D
);

  or or_1 (D, A, B, C);
endmodule

module _7_ii (
  input  A,
  input  B,
  input  C,
  output out_4
);

  wire and_1_out;

  and and_1 (and_1_out, A, B);
  or or_1 (out_4, and_1_out, C);
endmodule

module Que_8_a (
  input  A,
  input  B,
  input  C,
  input  D,
  input  E,
  input  F,
  output D_2
);

  wire and_1_out, nand_1_out, nand_2_out;

  nand nand_1 (nand_1_out, A, B);
  and and_1 (and_1_out, C, D);
  nand nand_2 (nand_2_out, E, F);
  or or_1 (D_2, nand_1_out, and_1_out, nand_2_out);
endmodule

module _8_b (
  input  X,
  input  Y,
  input  Z,
  output D
);

  wire not_1_out, or_1_out, or_2_out, or_3_out;

  not not_1 (not_1_out, X);
  or or_1 (or_1_out, not_1_out, Y);
  or or_2 (or_2_out, X, Z);
  or or_3 (or_3_out, Y, Z);
  and and_1 (D, or_1_out, or_2_out, or_3_out);
endmodule
